// Logisim project EPv7.circ as structural Verilog: 4 circuits, main circuit Contador
module Contador (
  input  Clock,
  output S1,
  output S2,
  output S3,
  output S4,
  output S5,
  output S6,
  output M1,
  output M2,
  output M3,
  output M4,
  output M5,
  output M6,
  output H1,
  output H2,
  output H3,
  output H4,
  output H5
);

  wire and_1_out, and_2_out, and_3_out, and_4_out, and_5_out, and_6_out, and_7_out, and_8_out, and_9_out,
       and_10_out, and_11_out, and_12_out, and_13_out, and_14_out, and_15_out, and_16_out, and_17_out,
       and_18_out, and_19_out, and_20_out, and_21_out, button_1_out, button_2_out, button_3_out, d_ff_1_q,
       d_ff_1_qn, j_k_ff_18_q, j_k_ff_18_qn, or_1_out, or_2_out, or_3_out, undriven;

  J_K_Flip_Flop #(.trigger("falling")) j_k_ff_1 (
    .J(1'b1), .clk(Clock), .K(1'b1), .Q(S1), .reset(or_2_out));  // open: Qn, preset, en
  J_K_Flip_Flop #(.trigger("falling")) j_k_ff_2 (
    .J(1'b1), .clk(and_17_out), .K(1'b1), .Q(M1), .preset(undriven), .en(undriven), .reset(or_3_out));  // open: Qn
  J_K_Flip_Flop #(.trigger("falling")) j_k_ff_3 (
    .J(1'b1), .clk(and_18_out), .K(1'b1), .Q(H1), .reset(or_1_out));  // open: Qn, preset, en
  J_K_Flip_Flop #(.trigger("falling")) j_k_ff_4 (
    .J(S1), .clk(Clock), .K(S1), .Q(S2), .reset(or_2_out));  // open: Qn, preset, en
  J_K_Flip_Flop #(.trigger("falling")) j_k_ff_5 (
    .J(M1), .clk(and_17_out), .K(M1), .Q(M2), .reset(or_3_out));  // open: Qn, preset, en
  J_K_Flip_Flop #(.trigger("falling")) j_k_ff_6 (
    .J(H1), .clk(and_18_out), .K(H1), .Q(H2), .reset(or_1_out));  // open: Qn, preset, en
  and and_1 (and_1_out, S1, S2);
  J_K_Flip_Flop #(.trigger("falling")) j_k_ff_7 (
    .J(and_1_out), .clk(Clock), .K(and_1_out), .Q(S3), .reset(or_2_out));  // open: Qn, preset, en
  and and_2 (and_2_out, M1, M2);
  J_K_Flip_Flop #(.trigger("falling")) j_k_ff_8 (
    .J(and_2_out), .clk(and_17_out), .K(and_2_out), .Q(M3), .reset(or_3_out));  // open: Qn, preset, en
  and and_3 (and_3_out, H1, H2);
  J_K_Flip_Flop #(.trigger("falling")) j_k_ff_9 (
    .J(and_3_out), .clk(and_18_out), .K(and_3_out), .Q(H3), .reset(or_1_out));  // open: Qn, preset, en
  and and_4 (and_4_out, and_1_out, S3);
  and and_5 (and_5_out, and_2_out, M3);
  and and_6 (and_6_out, and_3_out, H3);
  J_K_Flip_Flop #(.trigger("falling")) j_k_ff_10 (
    .J(and_4_out), .clk(Clock), .K(and_4_out), .Q(S4), .reset(or_2_out));  // open: Qn, preset, en
  J_K_Flip_Flop #(.trigger("falling")) j_k_ff_11 (
    .J(and_5_out), .clk(and_17_out), .K(and_5_out), .Q(M4), .reset(or_3_out));  // open: Qn, preset, en
  J_K_Flip_Flop #(.trigger("falling")) j_k_ff_12 (
    .J(and_6_out), .clk(and_18_out), .K(and_6_out), .Q(H4), .reset(or_1_out));  // open: Qn, preset, en
  and and_7 (and_7_out, S3, S4);
  and and_8 (and_8_out, and_4_out, S4);
  and and_9 (and_9_out, M3, M4);
  and and_10 (and_10_out, and_5_out, M4);
  and and_11 (and_11_out, and_6_out, H4);
  J_K_Flip_Flop #(.trigger("falling")) j_k_ff_13 (
    .J(and_8_out), .clk(Clock), .K(and_8_out), .Q(S5), .reset(or_2_out));  // open: Qn, preset, en
  J_K_Flip_Flop #(.trigger("falling")) j_k_ff_14 (
    .J(and_10_out), .clk(and_17_out), .K(and_10_out), .Q(M5), .reset(or_3_out));  // open: Qn, preset, en
  J_K_Flip_Flop #(.trigger("falling")) j_k_ff_15 (
    .J(and_11_out), .clk(and_18_out), .K(and_11_out), .Q(H5), .reset(or_1_out));  // open: Qn, preset, en
  and and_12 (and_12_out, and_8_out, S5);
  or or_1 (or_1_out, and_19_out, button_3_out);
  and and_13 (and_13_out, and_7_out, S5);
  J_K_Flip_Flop #(.trigger("falling")) j_k_ff_16 (
    .J(and_12_out), .clk(Clock), .K(and_12_out), .Q(S6), .reset(or_2_out));  // open: Qn, preset, en
  or or_2 (or_2_out, and_17_out, button_1_out);
  Button button_1 (.out(button_1_out));
  and and_14 (and_14_out, and_9_out, M5);
  and and_15 (and_15_out, and_10_out, M5);
  J_K_Flip_Flop #(.trigger("falling")) j_k_ff_17 (
    .J(and_15_out), .clk(and_17_out), .K(and_15_out), .Q(M6), .reset(or_3_out));  // open: Qn, preset, en
  or or_3 (or_3_out, and_18_out, button_2_out);
  and and_16 (and_16_out, H4, H5);
  and and_17 (and_17_out, Clock, and_20_out);
  and and_18 (and_18_out, Clock, and_21_out);
  Button button_2 (.out(button_2_out));
  and and_19 (and_19_out, Clock, and_16_out);
  Button button_3 (.out(button_3_out));
  and and_20 (and_20_out, and_13_out, S6);
  and and_21 (and_21_out, and_14_out, M6);
  D_Flip_Flop #(.trigger("falling")) d_ff_1 (
    .clk(and_20_out), .D(1'b1), .Q(d_ff_1_q), .Qn(d_ff_1_qn));  // open: preset, en, reset
  J_K_Flip_Flop #(.trigger("falling")) j_k_ff_18 (
    .J(1'b1), .clk(and_20_out), .K(1'b1), .Q(j_k_ff_18_q), .Qn(j_k_ff_18_qn));  // open: preset, en, reset

  // Notes on the sheet:
  //   Clock: pull=down
endmodule

module Decodificador_do_Display (
  input  A,
  input  B,
  input  C,
  input  D,
  output A_2,
  output B_2,
  output C_2,
  output D_2,
  output E,
  output F,
  output G
);

  wire and_1_out, and_2_out, and_3_out, and_4_out, and_5_out, and_6_out, and_7_out, and_8_out, and_9_out,
       and_10_out, and_11_out, and_12_out, and_13_out, and_14_out, and_15_out, and_16_out, and_17_out,
       and_18_out, and_19_out, and_20_out, and_21_out, and_22_out, and_23_out, and_24_out, and_25_out,
       and_26_out, and_27_out, not_1_out, not_2_out, not_3_out, not_4_out;

  not not_1 (not_1_out, D);
  not not_2 (not_2_out, C);
  not not_3 (not_3_out, A);
  not not_4 (not_4_out, B);
  and and_1 (and_1_out, C, not_3_out);
  and and_2 (and_2_out, not_2_out, A, not_4_out);
  and and_3 (and_3_out, not_1_out, not_2_out, not_4_out);
  and and_4 (and_4_out, D, not_3_out, B);
  and and_5 (and_5_out, not_3_out, not_4_out);
  and and_6 (and_6_out, not_4_out, not_2_out);
  and and_7 (and_7_out, not_1_out, not_2_out, not_3_out);
  and and_8 (and_8_out, C, not_3_out, D);
  and and_9 (and_9_out, not_3_out, B);
  and and_10 (and_10_out, not_3_out, not_2_out);
  and and_11 (and_11_out, not_4_out, not_2_out);
  and and_12 (and_12_out, not_3_out, D);
  and and_13 (and_13_out, A, not_4_out, not_2_out);
  and and_14 (and_14_out, not_3_out, not_4_out, C);
  and and_15 (and_15_out, C, not_3_out, not_1_out);
  and and_16 (and_16_out, not_4_out, not_1_out, not_2_out);
  and and_17 (and_17_out, not_2_out, B, not_3_out, D);
  and and_18 (and_18_out, not_4_out, not_2_out, not_1_out);
  and and_19 (and_19_out, not_3_out, not_1_out, C);
  and and_20 (and_20_out, not_2_out, not_4_out, A);
  and and_21 (and_21_out, B, not_3_out, not_2_out);
  and and_22 (and_22_out, not_2_out, not_4_out, not_1_out);
  and and_23 (and_23_out, not_3_out, B, not_1_out);
  and and_24 (and_24_out, A, not_2_out, not_4_out);
  and and_25 (and_25_out, not_2_out, B, not_3_out);
  and and_26 (and_26_out, C, not_3_out, not_4_out);
  and and_27 (and_27_out, C, not_1_out, not_3_out);
  or or_1 (A_2, and_1_out, and_2_out, and_3_out, and_4_out);
  or or_2 (B_2, and_5_out, and_6_out, and_7_out, and_8_out);
  or or_3 (C_2, and_9_out, and_10_out, and_11_out, and_12_out);
  or or_4 (D_2, and_13_out, and_14_out, and_15_out, and_16_out, and_17_out);
  or or_5 (E, and_18_out, and_19_out);
  or or_6 (F, and_20_out, and_21_out, and_22_out, and_23_out);
  or or_7 (G, and_24_out, and_25_out, and_26_out, and_27_out);
endmodule

module Tudo (
);

  wire clock_1_out, contador_1_h1, contador_1_h2, contador_1_h3, contador_1_h4, contador_1_h5, contador_1_m1,
       contador_1_m2, contador_1_m3, contador_1_m4, contador_1_m5, contador_1_m6, contador_1_s1,
       contador_1_s2, contador_1_s3, contador_1_s4, contador_1_s5, contador_1_s6,
       decodificador_do_display_1_a_2, decodificador_do_display_1_b_2, decodificador_do_display_1_c_2,
       decodificador_do_display_1_d_2, decodificador_do_display_1_e, decodificador_do_display_1_f,
       decodificador_do_display_1_g, decodificador_do_display_2_a_2, decodificador_do_display_2_b_2,
       decodificador_do_display_2_c_2, decodificador_do_display_2_d_2, decodificador_do_display_2_e,
       decodificador_do_display_2_f, decodificador_do_display_2_g, decodificador_do_display_3_a_2,
       decodificador_do_display_3_b_2, decodificador_do_display_3_c_2, decodificador_do_display_3_d_2,
       decodificador_do_display_3_e, decodificador_do_display_3_f, decodificador_do_display_3_g,
       decodificador_do_display_4_a_2, decodificador_do_display_4_b_2, decodificador_do_display_4_c_2,
       decodificador_do_display_4_d_2, decodificador_do_display_4_e, decodificador_do_display_4_f,
       decodificador_do_display_4_g, decodificador_do_display_5_a_2, decodificador_do_display_5_b_2,
       decodificador_do_display_5_c_2, decodificador_do_display_5_d_2, decodificador_do_display_5_e,
       decodificador_do_display_5_f, decodificador_do_display_5_g, decodificador_do_display_6_a_2,
       decodificador_do_display_6_b_2, decodificador_do_display_6_c_2, decodificador_do_display_6_d_2,
       decodificador_do_display_6_e, decodificador_do_display_6_f, decodificador_do_display_6_g,
       separador_decimal_1_d1, separador_decimal_1_d2, separador_decimal_1_d3, separador_decimal_1_d4,
       separador_decimal_1_u1, separador_decimal_1_u2, separador_decimal_1_u3, separador_decimal_1_u4,
       separador_decimal_2_d1, separador_decimal_2_d2, separador_decimal_2_d3, separador_decimal_2_d4,
       separador_decimal_2_u1, separador_decimal_2_u2, separador_decimal_2_u3, separador_decimal_2_u4,
       separador_decimal_3_d1, separador_decimal_3_d2, separador_decimal_3_d3, separador_decimal_3_d4,
       separador_decimal_3_u1, separador_decimal_3_u2, separador_decimal_3_u3, separador_decimal_3_u4;

  Clock clock_1 (.out(clock_1_out));
  Contador contador_1 (
    .Clock(clock_1_out), .M1(contador_1_m1), .S1(contador_1_s1), .H1(contador_1_h1), .S2(contador_1_s2),
    .M2(contador_1_m2), .H2(contador_1_h2), .S3(contador_1_s3), .M3(contador_1_m3), .H3(contador_1_h3),
    .S4(contador_1_s4), .M4(contador_1_m4), .H4(contador_1_h4), .S5(contador_1_s5), .M5(contador_1_m5),
    .H5(contador_1_h5), .S6(contador_1_s6), .M6(contador_1_m6));
  Separador_Decimal separador_decimal_1 (
    .F(contador_1_s1), .E(contador_1_s2), .D(contador_1_s3), .C(contador_1_s4), .B(contador_1_s5),
    .A(contador_1_s6), .U1(separador_decimal_1_u1), .U2(separador_decimal_1_u2), .U3(separador_decimal_1_u3),
    .U4(separador_decimal_1_u4), .D1(separador_decimal_1_d1), .D2(separador_decimal_1_d2),
    .D3(separador_decimal_1_d3), .D4(separador_decimal_1_d4));
  Separador_Decimal separador_decimal_2 (
    .F(contador_1_m1), .E(contador_1_m2), .D(contador_1_m3), .C(contador_1_m4), .B(contador_1_m5),
    .A(contador_1_m6), .U1(separador_decimal_2_u1), .U2(separador_decimal_2_u2), .U3(separador_decimal_2_u3),
    .U4(separador_decimal_2_u4), .D1(separador_decimal_2_d1), .D2(separador_decimal_2_d2),
    .D3(separador_decimal_2_d3), .D4(separador_decimal_2_d4));
  Separador_Decimal separador_decimal_3 (
    .F(contador_1_h1), .E(contador_1_h2), .D(contador_1_h3), .C(contador_1_h4), .B(contador_1_h5), .A(1'b0),
    .U1(separador_decimal_3_u1), .U2(separador_decimal_3_u2), .U3(separador_decimal_3_u3),
    .U4(separador_decimal_3_u4), .D1(separador_decimal_3_d1), .D2(separador_decimal_3_d2),
    .D3(separador_decimal_3_d3), .D4(separador_decimal_3_d4));
  Decodificador_do_Display decodificador_do_display_1 (
    .A(separador_decimal_3_d4), .A_2(decodificador_do_display_1_a_2), .B(separador_decimal_3_d3),
    .B_2(decodificador_do_display_1_b_2), .C(separador_decimal_3_d2), .C_2(decodificador_do_display_1_c_2),
    .D(separador_decimal_3_d1), .D_2(decodificador_do_display_1_d_2), .E(decodificador_do_display_1_e),
    .F(decodificador_do_display_1_f), .G(decodificador_do_display_1_g));
  Decodificador_do_Display decodificador_do_display_2 (
    .A(separador_decimal_2_d4), .A_2(decodificador_do_display_2_a_2), .B(separador_decimal_2_d3),
    .B_2(decodificador_do_display_2_b_2), .C(separador_decimal_2_d2), .C_2(decodificador_do_display_2_c_2),
    .D(separador_decimal_2_d1), .D_2(decodificador_do_display_2_d_2), .E(decodificador_do_display_2_e),
    .F(decodificador_do_display_2_f), .G(decodificador_do_display_2_g));
  Decodificador_do_Display decodificador_do_display_3 (
    .A(separador_decimal_1_d4), .A_2(decodificador_do_display_3_a_2), .B(separador_decimal_1_d3),
    .B_2(decodificador_do_display_3_b_2), .C(separador_decimal_1_d2), .C_2(decodificador_do_display_3_c_2),
    .D(separador_decimal_1_d1), .D_2(decodificador_do_display_3_d_2), .E(decodificador_do_display_3_e),
    .F(decodificador_do_display_3_f), .G(decodificador_do_display_3_g));
  _7_Segment_Display u_7_segment_display_1 (
    .g(decodificador_do_display_1_g), .f(decodificador_do_display_1_f), .a(decodificador_do_display_1_a_2),
    .b(decodificador_do_display_1_b_2), .e(decodificador_do_display_1_e), .d(decodificador_do_display_1_d_2),
    .c(decodificador_do_display_1_c_2));  // open: dp
  _7_Segment_Display u_7_segment_display_2 (
    .g(decodificador_do_display_2_g), .f(decodificador_do_display_2_f), .a(decodificador_do_display_2_a_2),
    .b(decodificador_do_display_2_b_2), .e(decodificador_do_display_2_e), .d(decodificador_do_display_2_d_2),
    .c(decodificador_do_display_2_c_2));  // open: dp
  _7_Segment_Display u_7_segment_display_3 (
    .g(decodificador_do_display_3_g), .f(decodificador_do_display_3_f), .a(decodificador_do_display_3_a_2),
    .b(decodificador_do_display_3_b_2), .e(decodificador_do_display_3_e), .d(decodificador_do_display_3_d_2),
    .c(decodificador_do_display_3_c_2));  // open: dp
  Decodificador_do_Display decodificador_do_display_4 (
    .A(separador_decimal_3_u4), .A_2(decodificador_do_display_4_a_2), .B(separador_decimal_3_u3),
    .B_2(decodificador_do_display_4_b_2), .C(separador_decimal_3_u2), .C_2(decodificador_do_display_4_c_2),
    .D(separador_decimal_3_u1), .D_2(decodificador_do_display_4_d_2), .E(decodificador_do_display_4_e),
    .F(decodificador_do_display_4_f), .G(decodificador_do_display_4_g));
  Decodificador_do_Display decodificador_do_display_5 (
    .A(separador_decimal_2_u4), .A_2(decodificador_do_display_5_a_2), .B(separador_decimal_2_u3),
    .B_2(decodificador_do_display_5_b_2), .C(separador_decimal_2_u2), .C_2(decodificador_do_display_5_c_2),
    .D(separador_decimal_2_u1), .D_2(decodificador_do_display_5_d_2), .E(decodificador_do_display_5_e),
    .F(decodificador_do_display_5_f), .G(decodificador_do_display_5_g));
  Decodificador_do_Display decodificador_do_display_6 (
    .A(separador_decimal_1_u4), .A_2(decodificador_do_display_6_a_2), .B(separador_decimal_1_u3),
    .B_2(decodificador_do_display_6_b_2), .C(separador_decimal_1_u2), .C_2(decodificador_do_display_6_c_2),
    .D(separador_decimal_1_u1), .D_2(decodificador_do_display_6_d_2), .E(decodificador_do_display_6_e),
    .F(decodificador_do_display_6_f), .G(decodificador_do_display_6_g));
  _7_Segment_Display u_7_segment_display_4 (
    .g(decodificador_do_display_4_g), .f(decodificador_do_display_4_f), .a(decodificador_do_display_4_a_2),
    .b(decodificador_do_display_4_b_2), .e(decodificador_do_display_4_e), .d(decodificador_do_display_4_d_2),
    .c(decodificador_do_display_4_c_2));  // open: dp
  _7_Segment_Display u_7_segment_display_5 (
    .g(decodificador_do_display_5_g), .f(decodificador_do_display_5_f), .a(decodificador_do_display_5_a_2),
    .b(decodificador_do_display_5_b_2), .e(decodificador_do_display_5_e), .d(decodificador_do_display_5_d_2),
    .c(decodificador_do_display_5_c_2));  // open: dp
  _7_Segment_Display u_7_segment_display_6 (
    .g(decodificador_do_display_6_g), .f(decodificador_do_display_6_f), .a(decodificador_do_display_6_a_2),
    .b(decodificador_do_display_6_b_2), .e(decodificador_do_display_6_e), .d(decodificador_do_display_6_d_2),
    .c(decodificador_do_display_6_c_2));  // open: dp
endmodule

module Separador_Decimal (
  input  F,
  input  E,
  input  D,
  input  C,
  input  B,
  input  A,
  output U4,
  output U3,
  output U2,
  output U1,
  output D4,
  output D3,
  output D2,
  output D1
);

  wire and_1_out, and_2_out, and_3_out, and_4_out, and_5_out, and_6_out, and_7_out, and_8_out, and_9_out,
       and_10_out, and_11_out, and_12_out, and_13_out, and_14_out, and_15_out, and_16_out, and_17_out,
       and_18_out, and_19_out, and_20_out, and_21_out, and_22_out, and_23_out, and_24_out, and_25_out,
       and_26_out, and_27_out, and_28_out, and_29_out, and_30_out, and_31_out, and_32_out, and_33_out,
       and_34_out, and_35_out, and_36_out, and_37_out, and_38_out, and_39_out, not_1_out, not_2_out,
       not_3_out, not_4_out, not_5_out, not_6_out, or_3_out, or_4_out, or_5_out, or_6_out, or_7_out,
       or_8_out, or_9_out, or_10_out, or_11_out;

  not not_1 (not_1_out, B);
  not not_2 (not_2_out, A);
  not not_3 (not_3_out, D);
  not not_4 (not_4_out, C);
  not not_5 (not_5_out, F);
  not not_6 (not_6_out, E);
  and and_1 (and_1_out, A, not_1_out, C);
  and and_2 (and_2_out, A, B, not_3_out);
  and and_3 (and_3_out, A, B, not_4_out);
  and and_4 (and_4_out, A, not_1_out, not_4_out);
  and and_5 (and_5_out, not_2_out, B, D);
  and and_6 (and_6_out, not_2_out, B, C);
  and and_7 (and_7_out, not_2_out, not_1_out, C, D);
  and and_8 (and_8_out, A, B, not_4_out, D);
  and and_9 (and_9_out, A, not_1_out, not_4_out);
  and and_10 (and_10_out, not_2_out, B, not_4_out, not_3_out);
  and and_11 (and_11_out, A, B, C, not_3_out);
  and and_12 (and_12_out, not_2_out, not_1_out, C, not_3_out, E);
  and and_13 (and_13_out, not_2_out, B, C, D, E);
  and and_14 (and_14_out, A, B, not_4_out, not_3_out, E);
  and and_15 (and_15_out, not_2_out, not_1_out, C, not_3_out, not_6_out);
  and and_16 (and_16_out, not_2_out, B, not_4_out, not_3_out, E);
  and and_17 (and_17_out, not_2_out, B, C, D, not_6_out);
  and and_18 (and_18_out, A, not_1_out, not_4_out, D, E);
  and and_19 (and_19_out, A, B, not_4_out, not_3_out, not_6_out);
  and and_20 (and_20_out, A, B, C, not_3_out, E);
  and and_21 (and_21_out, not_2_out, not_1_out, not_4_out, D);
  and and_22 (and_22_out, not_2_out, not_1_out, C, D, E);
  and and_23 (and_23_out, not_2_out, B, not_4_out, not_3_out, not_6_out);
  and and_24 (and_24_out, not_2_out, B, C, not_3_out);
  and and_25 (and_25_out, A, not_1_out, not_4_out, not_3_out, E);
  and and_26 (and_26_out, A, not_1_out, not_4_out, D, not_6_out);
  and and_27 (and_27_out, A, not_1_out, C, D);
  and and_28 (and_28_out, A, B, not_4_out, D, E);
  and and_29 (and_29_out, A, B, C, not_3_out, not_6_out);
  and and_30 (and_30_out, A, not_1_out, C, E);
  and and_31 (and_31_out, not_2_out, not_1_out, not_4_out, E);
  and and_32 (and_32_out, not_2_out, not_4_out, D, E);
  and and_33 (and_33_out, not_2_out, B, C, not_3_out, E);
  and and_34 (and_34_out, A, not_1_out, not_4_out, not_6_out);
  and and_35 (and_35_out, not_2_out, not_1_out, C, D, not_6_out);
  and and_36 (and_36_out, A, B, not_4_out, D, not_6_out);
  and and_37 (and_37_out, not_2_out, B, not_4_out, not_3_out, not_6_out);
  and and_38 (and_38_out, A, B, not_4_out, D, not_6_out);
  and and_39 (and_39_out, A, B, C, not_3_out, not_6_out);
  or or_1 (D2, and_4_out, and_5_out, and_6_out);
  or or_2 (D3, and_1_out, and_2_out, and_3_out);
  or or_3 (or_3_out, and_7_out, and_8_out, and_9_out, and_10_out);
  or or_4 (or_4_out, and_11_out, and_12_out, and_13_out, and_14_out);
  or or_5 (or_5_out, and_15_out, and_16_out, and_17_out);
  or or_6 (or_6_out, and_18_out, and_19_out, and_20_out);
  or or_7 (or_7_out, and_21_out, and_22_out, and_23_out);
  or or_8 (or_8_out, and_24_out, and_25_out, and_26_out);
  or or_9 (or_9_out, and_27_out, and_28_out, and_29_out);
  or or_10 (or_10_out, and_30_out, and_31_out, and_32_out, and_33_out);
  or or_11 (or_11_out, and_36_out, and_34_out, and_35_out, and_37_out, and_38_out, and_39_out);
  or or_12 (U4, or_5_out, or_6_out);
  or or_13 (U3, or_7_out, or_8_out, or_9_out);
  or or_14 (U2, or_10_out, or_11_out);
  or or_15 (D1, or_3_out, or_4_out);

  assign D4 = 1'b0;
  assign U1 = F;
endmodule
