// Logisim project EPv9.circ as structural Verilog: 4 circuits, main circuit Contador
module Contador (
);

  wire and_1_out, and_2_out, and_3_out, and_4_out, and_5_out, and_6_out, and_7_out, and_8_out, and_9_out,
       and_10_out, clock_1_out, j_k_ff_1_q, j_k_ff_2_q, j_k_ff_3_q, j_k_ff_4_q, j_k_ff_5_q, j_k_ff_6_q,
       j_k_ff_7_q, j_k_ff_8_q, j_k_ff_9_q, j_k_ff_10_q, j_k_ff_11_q, not_1_out, not_2_out, not_3_out,
       not_4_out, xnor_1_out;

  Clock clock_1 (.out(clock_1_out));
  and and_1 (and_1_out, clock_1_out, j_k_ff_5_q);
  and and_2 (and_2_out, and_1_out, and_7_out);
  and and_3 (and_3_out, and_2_out, and_8_out);
  not not_1 (not_1_out, j_k_ff_5_q);
  not not_2 (not_2_out, and_7_out);
  not not_3 (not_3_out, and_8_out);
  and and_4 (and_4_out, clock_1_out, not_1_out);
  and and_5 (and_5_out, and_1_out, not_2_out);
  and and_6 (and_6_out, and_2_out, not_3_out);
  J_K_Flip_Flop #(.trigger("falling")) j_k_ff_1 (
    .J(1'b1), .clk(and_4_out), .K(1'b1), .Q(j_k_ff_1_q), .reset(and_9_out));  // open: Qn, preset, en
  J_K_Flip_Flop #(.trigger("falling")) j_k_ff_2 (
    .J(1'b1), .clk(and_5_out), .K(1'b1), .Q(j_k_ff_2_q), .reset(and_9_out));  // open: Qn, preset, en
  J_K_Flip_Flop #(.trigger("falling")) j_k_ff_3 (
    .J(1'b1), .clk(and_6_out), .K(1'b1), .Q(j_k_ff_3_q), .reset(and_9_out));  // open: Qn, preset, en
  J_K_Flip_Flop #(.trigger("falling")) j_k_ff_4 (
    .J(1'b1), .clk(and_3_out), .K(1'b1), .Q(j_k_ff_4_q), .reset(and_9_out));  // open: Qn, preset, en
  J_K_Flip_Flop #(.trigger("falling")) j_k_ff_5 (
    .J(1'b1), .clk(j_k_ff_1_q), .K(1'b1), .Q(j_k_ff_5_q), .reset(and_9_out));  // open: Qn, preset, en
  J_K_Flip_Flop #(.trigger("falling")) j_k_ff_6 (
    .J(1'b1), .clk(j_k_ff_2_q), .K(1'b1), .Q(j_k_ff_6_q), .reset(and_9_out));  // open: Qn, preset, en
  J_K_Flip_Flop #(.trigger("falling")) j_k_ff_7 (
    .J(1'b1), .clk(j_k_ff_3_q), .K(1'b1), .Q(j_k_ff_7_q), .reset(and_9_out));  // open: Qn, preset, en
  J_K_Flip_Flop #(.trigger("falling")) j_k_ff_8 (
    .J(1'b1), .clk(j_k_ff_4_q), .K(1'b1), .Q(j_k_ff_8_q), .reset(and_9_out));  // open: Qn, preset, en
  and and_7 (and_7_out, j_k_ff_2_q, j_k_ff_6_q);
  J_K_Flip_Flop #(.trigger("falling")) j_k_ff_9 (
    .J(1'b1), .clk(j_k_ff_7_q), .K(1'b1), .Q(j_k_ff_9_q), .reset(and_9_out));  // open: Qn, preset, en
  J_K_Flip_Flop #(.trigger("falling")) j_k_ff_10 (
    .J(1'b1), .clk(j_k_ff_8_q), .K(1'b1), .Q(j_k_ff_10_q), .reset(and_9_out));  // open: Qn, preset, en
  and and_8 (and_8_out, j_k_ff_3_q, j_k_ff_9_q);
  J_K_Flip_Flop #(.trigger("falling")) j_k_ff_11 (
    .J(1'b1), .clk(j_k_ff_10_q), .K(1'b1), .Q(j_k_ff_11_q), .reset(and_9_out));  // open: Qn, preset, en
  and and_9 (and_9_out, j_k_ff_8_q, j_k_ff_11_q);
  xnor xnor_1 (xnor_1_out, j_k_ff_5_q, and_7_out);
  not not_4 (not_4_out, and_8_out);
  and and_10 (and_10_out, xnor_1_out, not_4_out);
  LED led_1 (.in(and_10_out));
endmodule

module Decodificador_do_Display (
  input  A,
  input  B,
  input  C,
  input  D,
  output A_2,
  output B_2,
  output C_2,
  output D_2,
  output E,
  output F,
  output G
);

  wire and_1_out, and_2_out, and_3_out, and_4_out, and_5_out, and_6_out, and_7_out, and_8_out, and_9_out,
       and_10_out, and_11_out, and_12_out, and_13_out, and_14_out, and_15_out, and_16_out, and_17_out,
       and_18_out, and_19_out, and_20_out, and_21_out, and_22_out, and_23_out, and_24_out, and_25_out,
       and_26_out, and_27_out, not_1_out, not_2_out, not_3_out, not_4_out;

  not not_1 (not_1_out, D);
  not not_2 (not_2_out, C);
  not not_3 (not_3_out, A);
  not not_4 (not_4_out, B);
  and and_1 (and_1_out, C, not_3_out);
  and and_2 (and_2_out, not_2_out, A, not_4_out);
  and and_3 (and_3_out, not_1_out, not_2_out, not_4_out);
  and and_4 (and_4_out, D, not_3_out, B);
  and and_5 (and_5_out, not_3_out, not_4_out);
  and and_6 (and_6_out, not_4_out, not_2_out);
  and and_7 (and_7_out, not_1_out, not_2_out, not_3_out);
  and and_8 (and_8_out, C, not_3_out, D);
  and and_9 (and_9_out, not_3_out, B);
  and and_10 (and_10_out, not_3_out, not_2_out);
  and and_11 (and_11_out, not_4_out, not_2_out);
  and and_12 (and_12_out, not_3_out, D);
  and and_13 (and_13_out, A, not_4_out, not_2_out);
  and and_14 (and_14_out, not_3_out, not_4_out, C);
  and and_15 (and_15_out, C, not_3_out, not_1_out);
  and and_16 (and_16_out, not_4_out, not_1_out, not_2_out);
  and and_17 (and_17_out, not_2_out, B, not_3_out, D);
  and and_18 (and_18_out, not_4_out, not_2_out, not_1_out);
  and and_19 (and_19_out, not_3_out, not_1_out, C);
  and and_20 (and_20_out, not_2_out, not_4_out, A);
  and and_21 (and_21_out, B, not_3_out, not_2_out);
  and and_22 (and_22_out, not_2_out, not_4_out, not_1_out);
  and and_23 (and_23_out, not_3_out, B, not_1_out);
  and and_24 (and_24_out, A, not_2_out, not_4_out);
  and and_25 (and_25_out, not_2_out, B, not_3_out);
  and and_26 (and_26_out, C, not_3_out, not_4_out);
  and and_27 (and_27_out, C, not_1_out, not_3_out);
  or or_1 (A_2, and_1_out, and_2_out, and_3_out, and_4_out);
  or or_2 (B_2, and_5_out, and_6_out, and_7_out, and_8_out);
  or or_3 (C_2, and_9_out, and_10_out, and_11_out, and_12_out);
  or or_4 (D_2, and_13_out, and_14_out, and_15_out, and_16_out, and_17_out);
  or or_5 (E, and_18_out, and_19_out);
  or or_6 (F, and_20_out, and_21_out, and_22_out, and_23_out);
  or or_7 (G, and_24_out, and_25_out, and_26_out, and_27_out);
endmodule

module Tudo (
);

  wire clock_1_out, decodificador_do_display_1_a_2, decodificador_do_display_1_b_2,
       decodificador_do_display_1_c_2, decodificador_do_display_1_d_2, decodificador_do_display_1_e,
       decodificador_do_display_1_f, decodificador_do_display_1_g, decodificador_do_display_2_a_2,
       decodificador_do_display_2_b_2, decodificador_do_display_2_c_2, decodificador_do_display_2_d_2,
       decodificador_do_display_2_e, decodificador_do_display_2_f, decodificador_do_display_2_g,
       decodificador_do_display_3_a_2, decodificador_do_display_3_b_2, decodificador_do_display_3_c_2,
       decodificador_do_display_3_d_2, decodificador_do_display_3_e, decodificador_do_display_3_f,
       decodificador_do_display_3_g, decodificador_do_display_4_a_2, decodificador_do_display_4_b_2,
       decodificador_do_display_4_c_2, decodificador_do_display_4_d_2, decodificador_do_display_4_e,
       decodificador_do_display_4_f, decodificador_do_display_4_g, decodificador_do_display_5_a_2,
       decodificador_do_display_5_b_2, decodificador_do_display_5_c_2, decodificador_do_display_5_d_2,
       decodificador_do_display_5_e, decodificador_do_display_5_f, decodificador_do_display_5_g,
       decodificador_do_display_6_a_2, decodificador_do_display_6_b_2, decodificador_do_display_6_c_2,
       decodificador_do_display_6_d_2, decodificador_do_display_6_e, decodificador_do_display_6_f,
       decodificador_do_display_6_g, R_out, separador_decimal_1_d1, separador_decimal_1_d2,
       separador_decimal_1_d3, separador_decimal_1_d4, separador_decimal_1_u1, separador_decimal_1_u2,
       separador_decimal_1_u3, separador_decimal_1_u4, separador_decimal_2_d1, separador_decimal_2_d2,
       separador_decimal_2_d3, separador_decimal_2_d4, separador_decimal_2_u1, separador_decimal_2_u2,
       separador_decimal_2_u3, separador_decimal_2_u4, separador_decimal_3_d1, separador_decimal_3_d2,
       separador_decimal_3_d3, separador_decimal_3_d4, separador_decimal_3_u1, separador_decimal_3_u2,
       separador_decimal_3_u3, separador_decimal_3_u4, undriven, undriven_2, undriven_3, undriven_4,
       undriven_5, undriven_6, undriven_7, undriven_8, undriven_9, undriven_10, undriven_11, undriven_12,
       undriven_13, undriven_14, undriven_15, undriven_16, undriven_17;

  Clock clock_1 (.out(clock_1_out));
  Contador contador_1 ();
  Button R (.out(R_out));
  Separador_Decimal separador_decimal_1 (
    .F(undriven), .E(undriven_2), .D(undriven_3), .C(undriven_4), .B(undriven_5), .A(undriven_6),
    .U1(separador_decimal_1_u1), .U2(separador_decimal_1_u2), .U3(separador_decimal_1_u3),
    .U4(separador_decimal_1_u4), .D1(separador_decimal_1_d1), .D2(separador_decimal_1_d2),
    .D3(separador_decimal_1_d3), .D4(separador_decimal_1_d4));
  Separador_Decimal separador_decimal_2 (
    .F(undriven_7), .E(undriven_8), .D(undriven_9), .C(undriven_10), .B(undriven_11), .A(undriven_12),
    .U1(separador_decimal_2_u1), .U2(separador_decimal_2_u2), .U3(separador_decimal_2_u3),
    .U4(separador_decimal_2_u4), .D1(separador_decimal_2_d1), .D2(separador_decimal_2_d2),
    .D3(separador_decimal_2_d3), .D4(separador_decimal_2_d4));
  Separador_Decimal separador_decimal_3 (
    .F(undriven_13), .E(undriven_14), .D(undriven_15), .C(undriven_16), .B(undriven_17), .A(1'b0),
    .U1(separador_decimal_3_u1), .U2(separador_decimal_3_u2), .U3(separador_decimal_3_u3),
    .U4(separador_decimal_3_u4), .D1(separador_decimal_3_d1), .D2(separador_decimal_3_d2),
    .D3(separador_decimal_3_d3), .D4(separador_decimal_3_d4));
  Decodificador_do_Display decodificador_do_display_1 (
    .A(separador_decimal_3_d4), .A_2(decodificador_do_display_1_a_2), .B(separador_decimal_3_d3),
    .B_2(decodificador_do_display_1_b_2), .C(separador_decimal_3_d2), .C_2(decodificador_do_display_1_c_2),
    .D(separador_decimal_3_d1), .D_2(decodificador_do_display_1_d_2), .E(decodificador_do_display_1_e),
    .F(decodificador_do_display_1_f), .G(decodificador_do_display_1_g));
  Decodificador_do_Display decodificador_do_display_2 (
    .A(separador_decimal_2_d4), .A_2(decodificador_do_display_2_a_2), .B(separador_decimal_2_d3),
    .B_2(decodificador_do_display_2_b_2), .C(separador_decimal_2_d2), .C_2(decodificador_do_display_2_c_2),
    .D(separador_decimal_2_d1), .D_2(decodificador_do_display_2_d_2), .E(decodificador_do_display_2_e),
    .F(decodificador_do_display_2_f), .G(decodificador_do_display_2_g));
  Decodificador_do_Display decodificador_do_display_3 (
    .A(separador_decimal_1_d4), .A_2(decodificador_do_display_3_a_2), .B(separador_decimal_1_d3),
    .B_2(decodificador_do_display_3_b_2), .C(separador_decimal_1_d2), .C_2(decodificador_do_display_3_c_2),
    .D(separador_decimal_1_d1), .D_2(decodificador_do_display_3_d_2), .E(decodificador_do_display_3_e),
    .F(decodificador_do_display_3_f), .G(decodificador_do_display_3_g));
  _7_Segment_Display u_7_segment_display_1 (
    .g(decodificador_do_display_1_g), .f(decodificador_do_display_1_f), .a(decodificador_do_display_1_a_2),
    .b(decodificador_do_display_1_b_2), .e(decodificador_do_display_1_e), .d(decodificador_do_display_1_d_2),
    .c(decodificador_do_display_1_c_2));  // open: dp
  _7_Segment_Display u_7_segment_display_2 (
    .g(decodificador_do_display_2_g), .f(decodificador_do_display_2_f), .a(decodificador_do_display_2_a_2),
    .b(decodificador_do_display_2_b_2), .e(decodificador_do_display_2_e), .d(decodificador_do_display_2_d_2),
    .c(decodificador_do_display_2_c_2));  // open: dp
  _7_Segment_Display u_7_segment_display_3 (
    .g(decodificador_do_display_3_g), .f(decodificador_do_display_3_f), .a(decodificador_do_display_3_a_2),
    .b(decodificador_do_display_3_b_2), .e(decodificador_do_display_3_e), .d(decodificador_do_display_3_d_2),
    .c(decodificador_do_display_3_c_2));  // open: dp
  Decodificador_do_Display decodificador_do_display_4 (
    .A(separador_decimal_3_u4), .A_2(decodificador_do_display_4_a_2), .B(separador_decimal_3_u3),
    .B_2(decodificador_do_display_4_b_2), .C(separador_decimal_3_u2), .C_2(decodificador_do_display_4_c_2),
    .D(separador_decimal_3_u1), .D_2(decodificador_do_display_4_d_2), .E(decodificador_do_display_4_e),
    .F(decodificador_do_display_4_f), .G(decodificador_do_display_4_g));
  Decodificador_do_Display decodificador_do_display_5 (
    .A(separador_decimal_2_u4), .A_2(decodificador_do_display_5_a_2), .B(separador_decimal_2_u3),
    .B_2(decodificador_do_display_5_b_2), .C(separador_decimal_2_u2), .C_2(decodificador_do_display_5_c_2),
    .D(separador_decimal_2_u1), .D_2(decodificador_do_display_5_d_2), .E(decodificador_do_display_5_e),
    .F(decodificador_do_display_5_f), .G(decodificador_do_display_5_g));
  Decodificador_do_Display decodificador_do_display_6 (
    .A(separador_decimal_1_u4), .A_2(decodificador_do_display_6_a_2), .B(separador_decimal_1_u3),
    .B_2(decodificador_do_display_6_b_2), .C(separador_decimal_1_u2), .C_2(decodificador_do_display_6_c_2),
    .D(separador_decimal_1_u1), .D_2(decodificador_do_display_6_d_2), .E(decodificador_do_display_6_e),
    .F(decodificador_do_display_6_f), .G(decodificador_do_display_6_g));
  _7_Segment_Display u_7_segment_display_4 (
    .g(decodificador_do_display_4_g), .f(decodificador_do_display_4_f), .a(decodificador_do_display_4_a_2),
    .b(decodificador_do_display_4_b_2), .e(decodificador_do_display_4_e), .d(decodificador_do_display_4_d_2),
    .c(decodificador_do_display_4_c_2));  // open: dp
  _7_Segment_Display u_7_segment_display_5 (
    .g(decodificador_do_display_5_g), .f(decodificador_do_display_5_f), .a(decodificador_do_display_5_a_2),
    .b(decodificador_do_display_5_b_2), .e(decodificador_do_display_5_e), .d(decodificador_do_display_5_d_2),
    .c(decodificador_do_display_5_c_2));  // open: dp
  _7_Segment_Display u_7_segment_display_6 (
    .g(decodificador_do_display_6_g), .f(decodificador_do_display_6_f), .a(decodificador_do_display_6_a_2),
    .b(decodificador_do_display_6_b_2), .e(decodificador_do_display_6_e), .d(decodificador_do_display_6_d_2),
    .c(decodificador_do_display_6_c_2));  // open: dp

  // Notes on the sheet:
  //   Resetar
  //   Hora
  //   Minuto
  //   Segundo
endmodule

module Separador_Decimal (
  input  F,
  input  E,
  input  D,
  input  C,
  input  B,
  input  A,
  output U4,
  output U3,
  output U2,
  output U1,
  output D4,
  output D3,
  output D2,
  output D1
);

  wire and_1_out, and_2_out, and_3_out, and_4_out, and_5_out, and_6_out, and_7_out, and_8_out, and_9_out,
       and_10_out, and_11_out, and_12_out, and_13_out, and_14_out, and_15_out, and_16_out, and_17_out,
       and_18_out, and_19_out, and_20_out, and_21_out, and_22_out, and_23_out, and_24_out, and_25_out,
       and_26_out, and_27_out, and_28_out, and_29_out, and_30_out, and_31_out, and_32_out, and_33_out,
       and_34_out, and_35_out, and_36_out, and_37_out, and_38_out, and_39_out, not_1_out, not_2_out,
       not_3_out, not_4_out, not_5_out, not_6_out, or_3_out, or_4_out, or_5_out, or_6_out, or_7_out,
       or_8_out, or_9_out, or_10_out, or_11_out;

  not not_1 (not_1_out, B);
  not not_2 (not_2_out, A);
  not not_3 (not_3_out, D);
  not not_4 (not_4_out, C);
  not not_5 (not_5_out, F);
  not not_6 (not_6_out, E);
  and and_1 (and_1_out, A, not_1_out, C);
  and and_2 (and_2_out, A, B, not_3_out);
  and and_3 (and_3_out, A, B, not_4_out);
  and and_4 (and_4_out, A, not_1_out, not_4_out);
  and and_5 (and_5_out, not_2_out, B, D);
  and and_6 (and_6_out, not_2_out, B, C);
  and and_7 (and_7_out, not_2_out, not_1_out, C, D);
  and and_8 (and_8_out, A, B, not_4_out, D);
  and and_9 (and_9_out, A, not_1_out, not_4_out);
  and and_10 (and_10_out, not_2_out, B, not_4_out, not_3_out);
  and and_11 (and_11_out, A, B, C, not_3_out);
  and and_12 (and_12_out, not_2_out, not_1_out, C, not_3_out, E);
  and and_13 (and_13_out, not_2_out, B, C, D, E);
  and and_14 (and_14_out, A, B, not_4_out, not_3_out, E);
  and and_15 (and_15_out, not_2_out, not_1_out, C, not_3_out, not_6_out);
  and and_16 (and_16_out, not_2_out, B, not_4_out, not_3_out, E);
  and and_17 (and_17_out, not_2_out, B, C, D, not_6_out);
  and and_18 (and_18_out, A, not_1_out, not_4_out, D, E);
  and and_19 (and_19_out, A, B, not_4_out, not_3_out, not_6_out);
  and and_20 (and_20_out, A, B, C, not_3_out, E);
  and and_21 (and_21_out, not_2_out, not_1_out, not_4_out, D);
  and and_22 (and_22_out, not_2_out, not_1_out, C, D, E);
  and and_23 (and_23_out, not_2_out, B, not_4_out, not_3_out, not_6_out);
  and and_24 (and_24_out, not_2_out, B, C, not_3_out);
  and and_25 (and_25_out, A, not_1_out, not_4_out, not_3_out, E);
  and and_26 (and_26_out, A, not_1_out, not_4_out, D, not_6_out);
  and and_27 (and_27_out, A, not_1_out, C, D);
  and and_28 (and_28_out, A, B, not_4_out, D, E);
  and and_29 (and_29_out, A, B, C, not_3_out, not_6_out);
  and and_30 (and_30_out, A, not_1_out, C, E);
  and and_31 (and_31_out, not_2_out, not_1_out, not_4_out, E);
  and and_32 (and_32_out, not_2_out, not_4_out, D, E);
  and and_33 (and_33_out, not_2_out, B, C, not_3_out, E);
  and and_34 (and_34_out, A, not_1_out, not_4_out, not_6_out);
  and and_35 (and_35_out, not_2_out, not_1_out, C, D, not_6_out);
  and and_36 (and_36_out, A, B, not_4_out, D, not_6_out);
  and and_37 (and_37_out, not_2_out, B, not_4_out, not_3_out, not_6_out);
  and and_38 (and_38_out, A, B, not_4_out, D, not_6_out);
  and and_39 (and_39_out, A, B, C, not_3_out, not_6_out);
  or or_1 (D2, and_4_out, and_5_out, and_6_out);
  or or_2 (D3, and_1_out, and_2_out, and_3_out);
  or or_3 (or_3_out, and_7_out, and_8_out, and_9_out, and_10_out);
  or or_4 (or_4_out, and_11_out, and_12_out, and_13_out, and_14_out);
  or or_5 (or_5_out, and_15_out, and_16_out, and_17_out);
  or or_6 (or_6_out, and_18_out, and_19_out, and_20_out);
  or or_7 (or_7_out, and_21_out, and_22_out, and_23_out);
  or or_8 (or_8_out, and_24_out, and_25_out, and_26_out);
  or or_9 (or_9_out, and_27_out, and_28_out, and_29_out);
  or or_10 (or_10_out, and_30_out, and_31_out, and_32_out, and_33_out);
  or or_11 (or_11_out, and_36_out, and_34_out, and_35_out, and_37_out, and_38_out, and_39_out);
  or or_12 (U4, or_5_out, or_6_out);
  or or_13 (U3, or_7_out, or_8_out, or_9_out);
  or or_14 (U2, or_10_out, or_11_out);
  or or_15 (D1, or_3_out, or_4_out);

  assign D4 = 1'b0;
  assign U1 = F;
endmodule
