// Logisim project Ep Clodo 15.circ as structural Verilog: 1 circuit, main circuit main
module main (
  input  X
);

  wire and_1_out, and_2_out, and_3_out, and_4_out, and_5_out, and_6_out, and_7_out, and_8_out, and_9_out,
       and_10_out, and_11_out, and_12_out, and_13_out, and_14_out, and_15_out, and_16_out, and_17_out,
       and_18_out, clock_1_out, d_ff_1_q, d_ff_1_qn, d_ff_2_q, d_ff_2_qn, d_ff_3_q, d_ff_3_qn, d_ff_4_q,
       d_ff_4_qn, d_ff_5_q, multiplexer_1_out, multiplexer_2_out, multiplexer_3_out, multiplexer_4_out,
       or_1_out, or_2_out, or_3_out, or_4_out, or_5_out, xor_1_out;

  Clock clock_1 (.out(clock_1_out));
  and and_1 (and_1_out, d_ff_4_q, d_ff_3_qn);
  and and_2 (and_2_out, d_ff_4_q, d_ff_2_qn);
  and and_3 (and_3_out, d_ff_4_q, d_ff_1_qn);
  and and_4 (and_4_out, d_ff_4_qn, d_ff_3_q, d_ff_2_q, d_ff_1_q);
  or or_1 (or_1_out, d_ff_4_qn, d_ff_3_qn, d_ff_2_qn, d_ff_1_qn);
  or or_2 (or_2_out, and_1_out, and_2_out, and_3_out, and_4_out);
  Multiplexer #(.enable("false")) multiplexer_1 (.in0(or_2_out), .in1(or_1_out), .out(multiplexer_1_out), .sel(X));
  and and_5 (and_5_out, d_ff_4_qn, d_ff_3_qn);
  and and_6 (and_6_out, d_ff_3_q, d_ff_1_qn);
  and and_7 (and_7_out, d_ff_1_q, d_ff_2_qn);
  and and_8 (and_8_out, d_ff_3_qn, d_ff_2_q, d_ff_1_q);
  D_Flip_Flop d_ff_1 (
    .clk(clock_1_out), .D(multiplexer_4_out), .Q(d_ff_1_q), .Qn(d_ff_1_qn), .reset(and_18_out));  // open: preset, en
  or or_3 (or_3_out, and_5_out, and_6_out, and_7_out, and_8_out);
  Multiplexer #(.enable("false")) multiplexer_2 (.in0(or_3_out), .in1(or_1_out), .out(multiplexer_2_out), .sel(X));
  D_Flip_Flop d_ff_2 (
    .clk(clock_1_out), .D(multiplexer_3_out), .Q(d_ff_2_q), .Qn(d_ff_2_qn), .reset(and_18_out));  // open: preset, en
  and and_9 (and_9_out, d_ff_4_qn, d_ff_3_qn);
  and and_10 (and_10_out, d_ff_4_qn, d_ff_2_qn);
  and and_11 (and_11_out, d_ff_1_q, d_ff_3_qn);
  and and_12 (and_12_out, d_ff_2_qn, d_ff_2_q);
  D_Flip_Flop d_ff_3 (
    .clk(clock_1_out), .D(multiplexer_2_out), .Q(d_ff_3_q), .Qn(d_ff_3_qn), .reset(and_18_out));  // open: preset, en
  and and_13 (and_13_out, d_ff_4_q, d_ff_3_q);
  xor xor_1 (xor_1_out, d_ff_1_q, d_ff_2_q);
  and and_14 (and_14_out, and_13_out, xor_1_out);
  or or_4 (or_4_out, and_9_out, and_10_out, and_11_out, and_12_out);
  Multiplexer #(.enable("false")) multiplexer_3 (.in0(or_4_out), .in1(and_14_out), .out(multiplexer_3_out), .sel(X));
  D_Flip_Flop d_ff_4 (
    .clk(clock_1_out), .D(multiplexer_1_out), .Q(d_ff_4_q), .Qn(d_ff_4_qn), .reset(and_18_out));  // open: preset, en
  and and_15 (and_15_out, d_ff_4_qn, d_ff_3_q, d_ff_2_q);
  and and_16 (and_16_out, d_ff_4_q, d_ff_1_qn);
  D_Flip_Flop d_ff_5 (.clk(clock_1_out), .D(and_17_out), .Q(d_ff_5_q), .reset(and_18_out));  // open: Qn, preset, en
  and and_17 (and_17_out, d_ff_4_q, d_ff_3_q, d_ff_2_q, d_ff_1_q);
  or or_5 (or_5_out, and_15_out, and_16_out);
  Multiplexer #(.enable("false")) multiplexer_4 (.in0(or_5_out), .in1(d_ff_1_qn), .out(multiplexer_4_out), .sel(X));
  and and_18 (and_18_out, d_ff_5_q, and_17_out);
  LED led_1 (.in(and_18_out));

  // Notes on the sheet:
  //   E
  //   D
  //   C
  //   B
  //   A
endmodule
