// Logisim project Ep Clodo 19.circ as structural Verilog: 1 circuit, main circuit main
module main (
);

  wire and_1_out, and_2_out, and_3_out, clock_1_out, j_k_ff_1_qn, j_k_ff_2_qn, j_k_ff_3_q, j_k_ff_4_qn,
       or_1_out, or_2_out;

  Clock clock_1 (.out(clock_1_out));
  J_K_Flip_Flop j_k_ff_1 (.J(1'b1), .clk(clock_1_out), .K(1'b1), .Qn(j_k_ff_1_qn));  // open: Q, preset, en, reset
  and and_1 (and_1_out, j_k_ff_3_q, j_k_ff_4_qn);
  or or_1 (or_1_out, j_k_ff_1_qn, and_1_out);
  J_K_Flip_Flop j_k_ff_2 (
    .J(j_k_ff_1_qn), .clk(clock_1_out), .K(or_1_out), .Qn(j_k_ff_2_qn));  // open: Q, preset, en, reset
  and and_2 (and_2_out, j_k_ff_1_qn, j_k_ff_2_qn);
  and and_3 (and_3_out, j_k_ff_1_qn, j_k_ff_2_qn, j_k_ff_4_qn);
  J_K_Flip_Flop j_k_ff_3 (
    .J(and_3_out), .clk(clock_1_out), .K(j_k_ff_4_qn), .Q(j_k_ff_3_q));  // open: Qn, preset, en, reset
  or or_2 (or_2_out, j_k_ff_3_q, and_2_out);
  J_K_Flip_Flop j_k_ff_4 (
    .J(or_2_out), .clk(clock_1_out), .K(and_2_out), .Qn(j_k_ff_4_qn));  // open: Q, preset, en, reset

  // Notes on the sheet:
  //   D
  //   C
  //   B
  //   A
endmodule
