// Logisim project Ep Clodo 23.circ as structural Verilog: 2 circuits, main circuit main
module main (
  input  E1,
  input  E2
);

  wire and_1_out, and_2_out, and_3_out, and_4_out, and_5_out, and_6_out, and_7_out, clock_1_out, d_ff_1_q,
       not_1_out, not_2_out, not_3_out, not_4_out, temporizador_1_out_4, temporizador_2_out_4,
       temporizador_3_out_4, temporizador_4_out_4, Temporizador_5_out_4, temporizador_6_out_4;

  Clock clock_1 (.out(clock_1_out));
  and and_1 (and_1_out, clock_1_out, E1);
  and and_2 (and_2_out, E2, clock_1_out);
  and and_3 (and_3_out, and_1_out, and_2_out);
  D_Flip_Flop d_ff_1 (.clk(clock_1_out), .D(and_2_out), .Q(d_ff_1_q));  // open: Qn, preset, en, reset
  and and_4 (and_4_out, and_2_out, not_1_out);
  not not_1 (not_1_out, d_ff_1_q);
  Temporizador temporizador_1 (.out_4(temporizador_1_out_4), .in_1(and_4_out), .in_2(and_1_out));  // open: in_3
  not not_2 (not_2_out, temporizador_1_out_4);
  Temporizador temporizador_2 (.out_4(temporizador_2_out_4), .in_1(and_4_out), .in_2(not_2_out));  // open: in_3
  Temporizador temporizador_3 (.out_4(temporizador_3_out_4), .in_1(and_4_out), .in_2(not_2_out));  // open: in_3
  and and_5 (and_5_out, and_3_out, temporizador_2_out_4);
  and and_6 (and_6_out, and_3_out, temporizador_4_out_4);
  Temporizador temporizador_4 (.out_4(temporizador_4_out_4), .in_1(and_4_out), .in_2(not_3_out));  // open: in_3
  Temporizador Temporizador_5 (.out_4(Temporizador_5_out_4), .in_1(and_4_out), .in_2(not_3_out));  // open: in_3
  not not_3 (not_3_out, temporizador_3_out_4);
  Temporizador temporizador_6 (.out_4(temporizador_6_out_4), .in_1(and_4_out), .in_2(not_4_out));  // open: in_3
  not not_4 (not_4_out, Temporizador_5_out_4);
  and and_7 (and_7_out, and_3_out, temporizador_6_out_4);

  // Notes on the sheet:
  //   Temporizador
  //   2s
  //   Reset
  //   L1
  //   Temporizador
  //   10S
  //   Temporizador
  //   1s
  //   L2
  //   Temporizador
  //           10S
  //   1S
  //   Temporizador
  //   10s
  //   L3
endmodule

module Temporizador (
  input  in_1,
  input  in_2,
  input  in_3,
  output out_4
);

  and and_1 (in_1, in_2, in_3, 1'b0);

  assign out_4 = in_1;
endmodule
